// Logisim project 124.circ as structural Verilog: 3 circuits, main circuit main
module main (
  input  CLEAR,
  input  in_2,
  input  in_3,
  input  in_4
);

  wire CLK, LD_A, LD_B, LD_NULL1, LD_NULL2, LD_NULL3, LD_NULL4, LD_NULL5, LD_NULL6, LD_RAM_ADRESS,
       LD_RAM_DATA, LD_RESULT, LD_ROM_DATA_ADRESS, LD_ROM_DATA_DATA, LD_ROM_INST_ARESS, LD_ROM_INST_DATA,
       nor_1_out, nor_2_out, WR_A, WR_B, WR_NULL1, WR_NULL2, WR_NULL3, WR_NULL4, WR_NULL5, WR_NULL6,
       WR_RAM_ADRESS, WR_RAM_DATA, WR_RESULT, WR_ROM_DATA_ADRESS, WR_ROM_DATA_DATA, WR_ROM_INST_ARESS,
       WR_ROM_INST_DATA;
  wire [3:0] rom_1_data;
  wire [15:0] A_q, adres_unit_1_adres_out, arithmetic_unit_1_c, B_q, register_1_q;
  wire [15:4] rom_1_data_2;

  Clock clock_1 (.out(CLK));
  Register #(.width(16)) register_1 (.D(adres_unit_1_adres_out), .en(in_4), .Q(register_1_q), .clk(CLK), .clr(CLEAR));
  adres_unit adres_unit_1 (.ADRES_IN(register_1_q), .INSTRUCTION(rom_1_data), .ADRES_OUT(adres_unit_1_adres_out));
  ROM #(.addrWidth(16), .dataWidth(16)) rom_1 (.addr(register_1_q), .data({rom_1_data_2, rom_1_data}), .sel(1'b1));
  Register #(.width(16)) A (.en(in_3), .Q(A_q), .clk(CLK), .clr(CLEAR));  // open: D
  Register #(.width(16)) B (.en(in_2), .Q(B_q), .clk(CLK), .clr(CLEAR));  // open: D
  Decoder #(.select(4)) decoder_1 (
    .out0(LD_ROM_DATA_ADRESS), .out1(LD_ROM_DATA_DATA), .out2(LD_ROM_INST_ARESS), .out3(LD_ROM_INST_DATA),
    .out4(LD_RAM_ADRESS), .out5(LD_RAM_DATA), .out6(LD_A), .out7(LD_B), .out8(LD_RESULT), .out9(LD_NULL1),
    .out10(LD_NULL2), .out11(LD_NULL3), .out12(LD_NULL4), .out13(LD_NULL5), .out14(LD_NULL5),
    .out15(LD_NULL6), .sel(rom_1_data_2[7:4]), .en(nor_1_out));
  nor nor_1 (nor_1_out, rom_1_data_2[15], rom_1_data_2[14], rom_1_data_2[13], rom_1_data_2[12]);
  Arithmetic_Unit arithmetic_unit_1 (
    .A(A_q), .B(B_q), .EN(rom_1_data_2[15]), .Choise(rom_1_data_2[14:12]), .C(arithmetic_unit_1_c));  // open: Cin, Cout
  Register #(.width(16)) RESULT (.D(arithmetic_unit_1_c), .en(rom_1_data_2[15]), .clk(CLK), .clr(CLEAR));  // open: Q
  Decoder #(.select(4)) decoder_2 (
    .out0(WR_ROM_DATA_ADRESS), .out1(WR_ROM_DATA_DATA), .out2(WR_ROM_INST_ARESS), .out3(WR_ROM_INST_DATA),
    .out4(WR_RAM_ADRESS), .out5(WR_RAM_DATA), .out6(WR_A), .out7(WR_B), .out8(WR_RESULT), .out9(WR_NULL1),
    .out10(WR_NULL2), .out11(WR_NULL3), .out12(WR_NULL4), .out13(WR_NULL5), .out14(WR_NULL5),
    .out15(WR_NULL6), .sel(rom_1_data_2[11:8]), .en(nor_2_out));
  nor nor_2 (nor_2_out, rom_1_data_2[15], rom_1_data_2[14], rom_1_data_2[13], rom_1_data_2[12]);

  // Other names for the same wires on the sheet: EN_A = in_2; EN_B = in_3

  // Notes on the sheet:
  //   contents of rom_1 (hex, n*v repeats v):
  //   c002 b009 9001 d00a
endmodule

module Arithmetic_Unit (
  input  [15:0] A,
  input  [15:0] B,
  input  [15:0] Cin,
  input  EN,
  input  [2:0] Choise,
  output [15:0] C,
  output [15:0] Cout
);

  wire and_2_out;
  wire [0:0] adder_1_cout, subtractor_1_bout;
  wire [15:0] adder_1_out, and_1_out, divider_1_out, divider_1_rem, multiplier_1_cout, multiplier_1_out,
       not_1_out, or_1_out, subtractor_1_out, xor_1_out;

  assign not_1_out = ~A;  // NOT_Gate not_1, 16 bits wide
  assign and_1_out = A & B;  // AND_Gate and_1, 16 bits wide
  assign or_1_out = A | B;  // OR_Gate or_1, 16 bits wide
  assign xor_1_out = A ^ B;  // XOR_Gate xor_1, 16 bits wide
  Adder #(.width(16)) adder_1 (.a(A), .b(B), .out(adder_1_out), .cin(Cin[0]), .cout(adder_1_cout[0]));
  Subtractor #(.width(16)) subtractor_1 (
    .a(A), .b(B), .out(subtractor_1_out), .bin(Cin[0]), .bout(subtractor_1_bout[0]));
  Multiplier #(.width(16)) multiplier_1 (.a(A), .b(B), .out(multiplier_1_out), .cin(Cin), .cout(multiplier_1_cout));
  Divider #(.width(16)) divider_1 (.a(A), .b(B), .out(divider_1_out), .upper(Cin), .rem(divider_1_rem));
  Multiplexer #(.select(3), .width(16)) multiplexer_1 (
    .in0(not_1_out), .in1(and_1_out), .in2(or_1_out), .in3(xor_1_out), .in4(adder_1_out),
    .in5(subtractor_1_out), .in6(multiplier_1_out), .in7(divider_1_out), .out(C), .sel(Choise), .en(EN));
  and and_2 (and_2_out, Choise[2], EN);
  Multiplexer #(.select(2), .width(16)) multiplexer_2 (
    .in0({{15{1'b0}}, adder_1_cout[0]}), .in1({{15{1'b0}}, subtractor_1_bout[0]}), .in2(multiplier_1_cout),
    .in3(divider_1_rem), .out(Cout), .sel(Choise[1:0]), .en(and_2_out));
endmodule

module adres_unit (
  input  [15:0] ADRES_IN,
  input  [3:0] INSTRUCTION,
  output [15:0] ADRES_OUT
);

  wire [15:0] bit_extender_1_out, xor_1_out;

  assign bit_extender_1_out = {{13{1'b0}}, INSTRUCTION[2:0]};  // Bit_Extender bit_extender_1
  assign xor_1_out = bit_extender_1_out ^ {16{INSTRUCTION[3]}};  // XOR_Gate xor_1, 16 bits wide
  Adder #(.width(16)) adder_1 (.a(ADRES_IN), .b(xor_1_out), .out(ADRES_OUT), .cin(INSTRUCTION[3]));  // open: cout
endmodule
